# Fritzing sketch Adxl345(Untitled Sketch) (saved by Fritzing 0.9.3b)
breadboards: 1

parts:
  Raspberry_Pi_1 = Raspberry Pi 3 [part_number=RPI-3-V1.2]
  Part2 = Triple Axis Accelerometer Breakout - ADXL345
  R1 = Resistor [tolerance=±5% resistance=10k package=THT]  # not connected
  R2 = Resistor [tolerance=±5% resistance=10k package=THT]
  R3 = Resistor [tolerance=±5% resistance=10k package=THT]

nets:
  3V3: Raspberry_Pi_1.3v3, Raspberry_Pi_1.3V3, Part2.VCC, Part2.CS, Part2.SDO, R2.Pin_1, R3.Pin_1
  N1: Raspberry_Pi_1.GPIO2, Part2.SDA, R3.Pin_0
  N2: Raspberry_Pi_1.GPIO3, Part2.SCL, R2.Pin_0
  GND: Raspberry_Pi_1.GND, Part2.GND
